// Logisim project AOC2017.circ as structural Verilog: 12 circuits, main circuit day06ab
module spiralGen (
  input  Enable,
  input  Clk,
  input  Rst,
  output [31:0] X,
  output [31:0] Y,
  output [31:0] I
);

  wire and_1_out, and_2_out, and_3_out, and_4_out;
  wire [3:0] d_ff_q;
  wire [5:0] rom_1_data;
  wire [31:0] negator_1_out;

  and and_1 (and_1_out, rom_1_data[3], Enable);
  and and_2 (and_2_out, rom_1_data[2], Enable);
  and and_3 (and_3_out, rom_1_data[1], Enable);
  and and_4 (and_4_out, rom_1_data[0], Enable);
  D_Flip_Flop d_ff (.clk(Clk), .D(rom_1_data[4]), .Q(d_ff_q[0]), .en(Enable), .reset(Rst));  // open: Qn, preset
  D_Flip_Flop u_X (.clk(Clk), .D(rom_1_data[5]), .Q(d_ff_q[1]), .en(Enable), .reset(Rst));  // open: Qn, preset
  Counter #(.width(32), .max('hffffffff)) X_2 (
    .load(and_1_out), .count(and_2_out), .Q(X), .clk(Clk), .clr(Rst));  // open: D, carry
  Negator #(.width(32)) negator_1 (.in(Y), .out(negator_1_out));
  Counter #(.width(32), .max('hffffffff)) u_Y (
    .load(and_3_out), .count(and_4_out), .Q(Y), .clk(Clk), .clr(Rst));  // open: D, carry
  Counter #(.width(32), .max('hffffffff)) u_I (.count(Enable), .Q(I), .clk(Clk), .clr(Rst));  // open: load, D, carry
  Comparator #(.width(32)) comparator_1 (.a(X), .b(Y), .eq(d_ff_q[2]));  // open: gt, lt
  Comparator #(.width(32)) comparator_2 (.a(X), .b(negator_1_out), .eq(d_ff_q[3]));  // open: gt, lt
  // Probe on X
  // Probe on Y
  // Probe on I
  ROM #(.addrWidth(4), .dataWidth(6)) rom_1 (.addr(d_ff_q), .data(rom_1_data));  // open: sel

  // Notes on the sheet:
  //   contents of rom_1 (hex, n*v repeats v):
  //   3 11 2c 34 0 10 11 4 2c 34 20 30 4 10 20 30
endmodule

module ssvTokenizer (
  input  [6:0] ASCII,
  input  Enable,
  input  Available,
  input  Clk,
  input  Rst,
  output TokenP,
  output NumberP,
  output SpaceP,
  output NewlineP,
  output [31:0] Number,
  output RST_2,
  output Read
);

  wire and_1_out, comparator_1_eq, comparator_2_eq, comparator_3_eq, comparator_4_eq, HasNumber_q,
       nand_1_out, Negative_qn, not_1_out;
  wire [31:0] adder_1_out, bit_extender_1_out, multiplexer_1_out, multiplier_1_out, negator_1_out, Number_q;

  and and_1 (and_1_out, Enable, Available);
  and and_2 (Read, and_1_out, nand_1_out);
  nand nand_1 (nand_1_out, ~comparator_4_eq, HasNumber_q);  // NAND_Gate
  Comparator #(.width(7)) comparator_1 (.a(7'b0100000), .b(ASCII), .eq(comparator_1_eq));  // open: gt, lt
  Comparator #(.width(7)) comparator_2 (.a(7'b0001010), .b(ASCII), .eq(comparator_2_eq));  // open: gt, lt
  Comparator #(.width(7)) comparator_3 (.a(7'b0101101), .b(ASCII), .eq(comparator_3_eq));  // open: gt, lt
  assign bit_extender_1_out = {{28{1'b0}}, ASCII[3:0]};  // Bit_Extender bit_extender_1
  Comparator #(.width(3)) comparator_4 (.a(ASCII[6:4]), .b(3'b011), .eq(comparator_4_eq));  // open: gt, lt
  not not_1 (not_1_out, comparator_4_eq);
  D_Flip_Flop HasNumber (
    .clk(Clk), .D(comparator_4_eq), .Q(HasNumber_q), .en(and_1_out), .reset(Rst));  // open: Qn, preset
  and and_3 (NumberP, ~comparator_4_eq, HasNumber_q, Available);  // AND_Gate
  and and_4 (SpaceP, comparator_1_eq, ~HasNumber_q, Available);  // AND_Gate
  and and_5 (NewlineP, comparator_2_eq, ~HasNumber_q, Available);  // AND_Gate
  J_K_Flip_Flop Negative (
    .J(comparator_3_eq), .clk(Clk), .K(not_1_out), .Qn(Negative_qn), .en(Available), .reset(Rst));  // open: Q, preset
  Multiplier #(.width(32)) multiplier_1 (.a(Number_q), .b(32'ha), .out(multiplier_1_out));  // open: cin, cout
  or or_1 (TokenP, NumberP, SpaceP, NewlineP);
  Multiplexer #(.width(32), .enable("false")) multiplexer_1 (
    .in0({32{1'b0}}), .in1(adder_1_out), .out(multiplexer_1_out), .sel(comparator_4_eq));
  Adder #(.width(32)) adder_1 (.a(bit_extender_1_out), .b(multiplier_1_out), .out(adder_1_out));  // open: cin, cout
  Register #(.width(32)) u_Number (.D(multiplexer_1_out), .en(and_1_out), .Q(Number_q), .clk(Clk), .clr(Rst));
  Negator #(.width(32)) negator_1 (.in(Number_q), .out(negator_1_out));
  Multiplexer #(.width(32), .enable("false")) multiplexer_2 (
    .in0(negator_1_out), .in1(Number_q), .out(Number), .sel(Negative_qn));

  assign RST_2 = Rst;

  // Notes on the sheet:
  //   Enable: pull=up
endmodule

module day01a (
  input  RST,
  output [31:0] Result
);

  wire clock_1_out, comparator_1_eq, comparator_2_eq, j_k_ff_1_qn, keyboard_1_avail;
  wire [3:0] bit_extender_1_out, Fst_q, Last_q, SndLast_q;
  wire [6:0] keyboard_1_data;
  wire [31:0] adder_1_out, and_1_out, bit_extender_2_out, bit_extender_3_out, bit_extender_4_out, Subtotal_q;

  Keyboard keyboard_1 (.clk(clock_1_out), .clr(RST), .avail(keyboard_1_avail), .data(keyboard_1_data));  // open: re
  Clock clock_1 (.out(clock_1_out));
  Bit_Extender #(.in_width(7), .out_width(4)) bit_extender_1 (.in(keyboard_1_data), .out(bit_extender_1_out));
  J_K_Flip_Flop j_k_ff_1 (
    .J(keyboard_1_avail), .clk(clock_1_out), .K(1'b0), .Qn(j_k_ff_1_qn), .en(1'b1), .reset(RST));  // open: Q, preset
  Register #(.width(4)) Last (.D(bit_extender_1_out), .en(keyboard_1_avail), .Q(Last_q), .clk(clock_1_out), .clr(RST));
  Register #(.width(4)) SndLast (.D(Last_q), .en(keyboard_1_avail), .Q(SndLast_q), .clk(clock_1_out), .clr(RST));
  Register #(.width(4)) Fst (.D(bit_extender_1_out), .en(j_k_ff_1_qn), .Q(Fst_q), .clk(clock_1_out), .clr(RST));
  assign bit_extender_2_out = {{28{1'b0}}, Last_q};  // Bit_Extender bit_extender_2
  Comparator #(.width(4)) comparator_1 (.a(Last_q), .b(SndLast_q), .eq(comparator_1_eq));  // open: gt, lt
  Comparator #(.width(4)) comparator_2 (.a(Last_q), .b(Fst_q), .eq(comparator_2_eq));  // open: gt, lt
  assign bit_extender_3_out = {{28{1'b0}}, Fst_q};  // Bit_Extender bit_extender_3
  Adder #(.width(32)) adder_1 (.a(bit_extender_2_out), .b(Subtotal_q), .out(adder_1_out));  // open: cin, cout
  assign bit_extender_4_out = {{31{1'b0}}, comparator_2_eq};  // Bit_Extender bit_extender_4
  assign and_1_out = bit_extender_4_out & bit_extender_3_out;  // AND_Gate and_1, 32 bits wide
  Register #(.width(32)) Subtotal (.D(adder_1_out), .en(comparator_1_eq), .Q(Subtotal_q), .clk(clock_1_out), .clr(RST));
  Adder #(.width(32)) adder_2 (.a(Subtotal_q), .b(and_1_out), .out(Result));  // open: cin, cout
  // Probe on Result
endmodule

module day01b (
  input  RST,
  output [31:0] Result
);

  wire and_1_out, and_2_out, clock_1_out, comparator_1_eq, comparator_2_eq, keyboard_1_avail, not_1_out,
       not_2_out, not_3_out, or_1_out, t_ff_1_q;
  wire [3:0] bit_extender_1_out, controlled_buffer_1_out, register_1_q, register_2_q;
  wire [6:0] keyboard_1_data;
  wire [23:0] adder_1_out, controlled_buffer_2_out, counter_1_q, counter_2_q, shifter_1_out;
  wire [31:0] adder_2_out, bit_extender_2_out, Subtotal_q;

  Keyboard keyboard_1 (.clk(clock_1_out), .clr(RST), .avail(keyboard_1_avail), .data(keyboard_1_data));  // open: re
  Clock clock_1 (.out(clock_1_out));
  Bit_Extender #(.in_width(7), .out_width(4)) bit_extender_1 (.in(keyboard_1_data), .out(bit_extender_1_out));
  assign controlled_buffer_1_out = keyboard_1_avail ? bit_extender_1_out : 4'bz;  // Controlled_Buffer controlled_buffer_1
  assign controlled_buffer_2_out = keyboard_1_avail ? counter_1_q : 24'bz;  // Controlled_Buffer controlled_buffer_2
  Counter #(.width(24), .max('hffffff)) counter_1 (
    .count(keyboard_1_avail), .Q(counter_1_q), .clk(clock_1_out), .clr(RST));  // open: load, D, carry
  Shifter #(.width(24), .shift("lr")) shifter_1 (.in(counter_1_q), .\dist (5'b00001), .out(shifter_1_out));
  RAM #(.addrWidth(24), .dataWidth(4)) ram_1 (
    .addr(controlled_buffer_2_out), .data(controlled_buffer_1_out), .sel(1'b1), .clk(clock_1_out),
    .ld(not_1_out), .clr(RST));
  not not_1 (not_1_out, keyboard_1_avail);
  T_Flip_Flop t_ff_1 (.clk(clock_1_out), .T(1'b1), .Q(t_ff_1_q), .reset(or_1_out));  // open: Qn, preset, en
  or or_1 (or_1_out, keyboard_1_avail, RST);
  Counter #(.width(24), .max('hffffff)) counter_2 (
    .count(t_ff_1_q), .Q(counter_2_q), .clk(clock_1_out), .clr(or_1_out));  // open: load, D, carry
  Comparator #(.width(24)) comparator_1 (.a(counter_2_q), .b(shifter_1_out), .eq(comparator_1_eq));  // open: gt, lt
  Adder #(.width(24)) adder_1 (.a(shifter_1_out), .b(counter_2_q), .out(adder_1_out));  // open: cin, cout
  Multiplexer #(.width(24)) multiplexer_1 (
    .in0(adder_1_out), .in1(counter_2_q), .out(controlled_buffer_2_out), .sel(t_ff_1_q), .en(not_2_out));
  not not_2 (not_2_out, or_1_out);
  and and_1 (and_1_out, comparator_1_eq, t_ff_1_q);
  Register #(.width(4)) register_1 (
    .D(controlled_buffer_1_out), .en(t_ff_1_q), .Q(register_1_q), .clk(clock_1_out), .clr(or_1_out));
  Register #(.width(4)) register_2 (
    .D(controlled_buffer_1_out), .en(not_3_out), .Q(register_2_q), .clk(clock_1_out), .clr(or_1_out));
  not not_3 (not_3_out, t_ff_1_q);
  assign bit_extender_2_out = {{28{1'b0}}, register_1_q};  // Bit_Extender bit_extender_2
  Comparator #(.width(4)) comparator_2 (.a(register_1_q), .b(register_2_q), .eq(comparator_2_eq));  // open: gt, lt
  Adder #(.width(32)) adder_2 (.a(Subtotal_q), .b(bit_extender_2_out), .out(adder_2_out));  // open: cin, cout
  and and_2 (and_2_out, comparator_2_eq, ~t_ff_1_q);  // AND_Gate
  Register #(.width(32)) register_3 (.D(Subtotal_q), .en(and_1_out), .Q(Result), .clk(clock_1_out), .clr(or_1_out));
  Register #(.width(32)) Subtotal (.D(adder_2_out), .en(and_2_out), .Q(Subtotal_q), .clk(clock_1_out), .clr(or_1_out));
  // Probe on Result
endmodule

// 8
module day02a (
  input  RST,
  output [31:0] Result
);

  wire clock_1_out, comparator_1_lt, comparator_2_gt, d_ff_1_q, keyboard_1_avail, not_1_out, or_1_out,
       ssvtokenizer_1_newlinep, ssvtokenizer_1_numberp, ssvtokenizer_1_read, ssvtokenizer_1_rst_2;
  wire [1:0] priority_encoder_1_out, priority_encoder_2_out;
  wire [6:0] keyboard_1_data;
  wire [31:0] adder_1_out, Max_q, Min_q, multiplexer_1_out, multiplexer_2_out, ssvtokenizer_1_number,
       subtractor_1_out;

  Keyboard keyboard_1 (
    .clk(clock_1_out), .re(ssvtokenizer_1_read), .clr(ssvtokenizer_1_rst_2), .avail(keyboard_1_avail),
    .data(keyboard_1_data));
  ssvTokenizer ssvtokenizer_1 (
    .ASCII(keyboard_1_data), .Available(keyboard_1_avail), .Clk(clock_1_out), .Rst(RST),
    .Read(ssvtokenizer_1_read), .NumberP(ssvtokenizer_1_numberp), .NewlineP(ssvtokenizer_1_newlinep),
    .Number(ssvtokenizer_1_number), .RST_2(ssvtokenizer_1_rst_2));  // open: TokenP, SpaceP, Enable
  Clock clock_1 (.out(clock_1_out));
  D_Flip_Flop d_ff_1 (.clk(clock_1_out), .D(RST), .Q(d_ff_1_q), .preset(RST));  // open: Qn, en, reset
  or or_1 (or_1_out, d_ff_1_q, ssvtokenizer_1_newlinep);
  not not_1 (not_1_out, ssvtokenizer_1_numberp);
  Comparator #(.width(32), .mode("unsigned")) comparator_1 (
    .a(Max_q), .b(ssvtokenizer_1_number), .lt(comparator_1_lt));  // open: gt, eq
  Comparator #(.width(32), .mode("unsigned")) comparator_2 (
    .a(Min_q), .b(ssvtokenizer_1_number), .gt(comparator_2_gt));  // open: eq, lt
  Multiplexer #(.select(2), .width(32), .enable("false")) multiplexer_1 (
    .in0(Max_q), .in1(ssvtokenizer_1_number), .in2(Max_q), .in3({32{1'b0}}), .out(multiplexer_1_out),
    .sel(priority_encoder_1_out));
  Priority_Encoder #(.select(2), .disabled(0)) priority_encoder_1 (
    .in0(1'b1), .in1(comparator_1_lt), .in2(not_1_out), .in3(or_1_out), .out(priority_encoder_1_out));  // open: gs, en_out, en_in
  Multiplexer #(.select(2), .width(32), .enable("false")) multiplexer_2 (
    .in0(Min_q), .in1(ssvtokenizer_1_number), .in2(Min_q), .in3({32{1'b1}}), .out(multiplexer_2_out),
    .sel(priority_encoder_2_out));
  Priority_Encoder #(.select(2), .disabled(0)) priority_encoder_2 (
    .in0(1'b1), .in1(comparator_2_gt), .in2(not_1_out), .in3(or_1_out), .out(priority_encoder_2_out));  // open: gs, en_out, en_in
  Register #(.width(32)) Max (.D(multiplexer_1_out), .Q(Max_q), .clk(clock_1_out), .clr(RST));  // open: en
  Register #(.width(32)) Min (.D(multiplexer_2_out), .Q(Min_q), .clk(clock_1_out), .clr(RST));  // open: en
  Adder #(.width(32)) adder_1 (.a(Result), .b(subtractor_1_out), .out(adder_1_out));  // open: cin, cout
  Subtractor #(.width(32)) subtractor_1 (.a(Max_q), .b(Min_q), .out(subtractor_1_out));  // open: bin, bout
  Register #(.width(32)) Subtotal (
    .D(adder_1_out), .en(ssvtokenizer_1_newlinep), .Q(Result), .clk(clock_1_out), .clr(RST));
  // Probe on Result
endmodule

module day02b (
  input  RST,
  output [31:0] Result
);

  wire clock_1_out, comparator_2_eq, comparator_3_eq, keyboard_1_avail, not_1_out, or_1_out,
       priority_encoder_1_p2, priority_encoder_1_p5, ssvtokenizer_1_newlinep, ssvtokenizer_1_numberp,
       ssvtokenizer_1_read, ssvtokenizer_1_rst_2;
  wire [1:0] priority_encoder_1_p3, register_1_q, rom_1_data, rom_1_data_4;
  wire [4:0] rom_1_data_3;
  wire [4:2] rom_1_data_2;
  wire [6:0] keyboard_1_data;
  wire [23:0] controlled_buffer_2_out, Id_q, In_q, Iread_q, subtractor_1_out;
  wire [31:0] adder_1_out, controlled_buffer_1_out, d_q, divider_1_out, divider_1_rem, ssvtokenizer_1_number;

  Clock clock_1 (.out(clock_1_out));
  Keyboard keyboard_1 (
    .clk(clock_1_out), .re(ssvtokenizer_1_read), .clr(ssvtokenizer_1_rst_2), .avail(keyboard_1_avail),
    .data(keyboard_1_data));
  ssvTokenizer ssvtokenizer_1 (
    .ASCII(keyboard_1_data), .Available(keyboard_1_avail), .Clk(clock_1_out), .Rst(RST),
    .Read(ssvtokenizer_1_read), .NumberP(ssvtokenizer_1_numberp), .NewlineP(ssvtokenizer_1_newlinep),
    .Number(ssvtokenizer_1_number), .RST_2(ssvtokenizer_1_rst_2), .Enable(rom_1_data_4[1]));  // open: TokenP, SpaceP
  assign controlled_buffer_1_out = rom_1_data_4[1] ? ssvtokenizer_1_number : 32'bz;  // Controlled_Buffer controlled_buffer_1
  Counter #(.width(24), .max('hffffff)) Iread (
    .load(rom_1_data_4[0]), .count(ssvtokenizer_1_numberp), .Q(Iread_q), .clk(clock_1_out), .clr(RST));  // open: D, carry
  assign controlled_buffer_2_out = rom_1_data_4[1] ? Iread_q : 24'bz;  // Controlled_Buffer controlled_buffer_2
  or or_1 (or_1_out, ssvtokenizer_1_numberp, not_1_out);
  not not_1 (not_1_out, rom_1_data_4[1]);
  // Priority_Encoder #(.select(2)) priority_encoder_1: pin names not known; wires that end beside it: 1'b1, priority_encoder_1_p2, priority_encoder_1_p3, ssvtokenizer_1_newlinep, priority_encoder_1_p5
  Subtractor #(.width(24)) subtractor_1 (.a(Iread_q), .b(24'h1), .out(subtractor_1_out));  // open: bin, bout
  RAM #(.addrWidth(24), .dataWidth(32)) ram_1 (
    .addr(controlled_buffer_2_out), .data(controlled_buffer_1_out), .sel(or_1_out), .clk(clock_1_out),
    .ld(not_1_out), .clr(RST));
  Register #(.width(2)) register_1 (.D(rom_1_data), .Q(register_1_q), .clk(clock_1_out), .clr(RST));  // open: en
  // Probe on {register_1_q, priority_encoder_1_p3}
  // Probe on controlled_buffer_1_out
  Register #(.width(32)) d (.D(controlled_buffer_1_out), .en(rom_1_data_3[4]), .Q(d_q), .clk(clock_1_out), .clr(RST));
  Counter #(.width(24), .max('hffffff)) In (
    .load(rom_1_data_3[3]), .count(rom_1_data_3[2]), .Q(In_q), .clk(clock_1_out), .clr(RST));  // open: D, carry
  Counter #(.width(24), .max('hffffff)) Id (
    .load(rom_1_data_3[1]), .count(rom_1_data_3[0]), .Q(Id_q), .clk(clock_1_out), .clr(RST));  // open: D, carry
  ROM #(.addrWidth(4), .dataWidth(12)) rom_1 (
    .addr({register_1_q, priority_encoder_1_p3}),
    .data({rom_1_data_4, rom_1_data_3, rom_1_data_2, rom_1_data}));  // open: sel
  // Probe on {rom_1_data_4, rom_1_data_3, rom_1_data_2, rom_1_data}
  Divider #(.width(32)) divider_1 (
    .a(controlled_buffer_1_out), .b(d_q), .out(divider_1_out), .rem(divider_1_rem));  // open: upper
  Comparator #(.width(24)) comparator_1 (.a(subtractor_1_out), .b(In_q), .eq(priority_encoder_1_p2));  // open: gt, lt
  assign controlled_buffer_2_out = rom_1_data_2[3] ? In_q : 24'bz;  // Controlled_Buffer controlled_buffer_3
  Comparator #(.width(24)) comparator_2 (.a(In_q), .b(Id_q), .eq(comparator_2_eq));  // open: gt, lt
  assign controlled_buffer_2_out = rom_1_data_2[4] ? Id_q : 24'bz;  // Controlled_Buffer controlled_buffer_4
  Adder #(.width(32)) adder_1 (.a(divider_1_out), .b(Result), .out(adder_1_out));  // open: cin, cout
  Comparator #(.width(32)) comparator_3 (.a({32{1'b0}}), .b(divider_1_rem), .eq(comparator_3_eq));  // open: gt, lt
  and and_1 (priority_encoder_1_p5, ~comparator_2_eq, comparator_3_eq);  // AND_Gate
  Register #(.width(32)) Subtotal (.D(adder_1_out), .en(rom_1_data_2[2]), .Q(Result), .clk(clock_1_out), .clr(RST));
  // Probe on Result

  // Notes on the sheet:
  //   contents of rom_1 (hex, n*v repeats v):
  //   940 940 942 803 89 12a b 54c 311 13 13 13 4*3
endmodule

module day03a (
  input  [31:0] in_1,
  input  RST,
  output [31:0] out_3
);

  wire clock_1_out, comparator_1_gt;
  wire [31:0] adder_1_out, multiplexer_1_out, multiplexer_2_out, spiralgen_1_i, spiralgen_1_x, spiralgen_1_y,
       subtractor_1_out, subtractor_2_out;

  Clock clock_1 (.out(clock_1_out));
  // Probe on in_1
  spiralGen spiralgen_1 (
    .Enable(comparator_1_gt), .Clk(clock_1_out), .Rst(RST), .X(spiralgen_1_x), .Y(spiralgen_1_y),
    .I(spiralgen_1_i));
  // Probe on spiralgen_1_x
  Comparator #(.width(32)) comparator_1 (.a(in_1), .b(adder_1_out), .gt(comparator_1_gt));  // open: eq, lt
  Adder #(.width(32)) adder_1 (.a({32{1'b0}}), .b(spiralgen_1_i), .out(adder_1_out), .cin(1'b1));  // open: cout
  // Probe on spiralgen_1_y
  // Probe on adder_1_out
  Subtractor #(.width(32)) subtractor_1 (.a({32{1'b0}}), .b(spiralgen_1_x), .out(subtractor_1_out));  // open: bin, bout
  Subtractor #(.width(32)) subtractor_2 (.a({32{1'b0}}), .b(spiralgen_1_y), .out(subtractor_2_out));  // open: bin, bout
  Multiplexer #(.width(32), .enable("false")) multiplexer_1 (
    .in0(spiralgen_1_x), .in1(subtractor_1_out), .out(multiplexer_1_out), .sel(spiralgen_1_x[31]));
  Adder #(.width(32)) adder_2 (.a(multiplexer_1_out), .b(multiplexer_2_out), .out(out_3));  // open: cin, cout
  Multiplexer #(.width(32), .enable("false")) multiplexer_2 (
    .in0(spiralgen_1_y), .in1(subtractor_2_out), .out(multiplexer_2_out), .sel(spiralgen_1_y[31]));
  // Probe on out_3
endmodule

module day03b (
  input  [31:0] in_1,
  input  RST,
  output [31:0] out_3
);

  wire and_1_out, and_2_out, clock_1_out, comparator_1_eq, comparator_2_lt, counter_1_carry, j_k_ff_1_q,
       j_k_ff_1_qn, nand_1_out, not_1_out;
  wire [2:0] counter_1_q;
  wire [3:0] rom_1_data;
  wire [11:0] adder_1_out, adder_2_out, bit_extender_1_out, bit_extender_2_out, bit_extender_3_out,
       bit_extender_4_out;
  wire [23:0] multiplexer_1_out;
  wire [31:0] adder_3_out, multiplexer_2_out, register_1_q, spiralgen_1_x, spiralgen_1_y;

  Clock clock_1 (.out(clock_1_out));
  J_K_Flip_Flop j_k_ff_1 (
    .J(counter_1_carry), .clk(clock_1_out), .K(not_1_out), .Q(j_k_ff_1_q), .Qn(j_k_ff_1_qn), .reset(RST));  // open: preset, en
  and and_1 (and_1_out, j_k_ff_1_q, not_1_out);
  Counter #(.width(3), .max('h7)) counter_1 (
    .count(j_k_ff_1_qn), .Q(counter_1_q), .carry(counter_1_carry), .clk(clock_1_out), .clr(RST));  // open: load, D
  Bit_Extender #(.in_width(32), .out_width(12), .\type ("sign")) bit_extender_1 (
    .in(spiralgen_1_x), .out(bit_extender_1_out));
  spiralGen spiralgen_1 (
    .Enable(and_1_out), .Clk(clock_1_out), .Rst(RST), .X(spiralgen_1_x), .Y(spiralgen_1_y));  // open: I
  Bit_Extender #(.in_width(32), .out_width(12), .\type ("sign")) bit_extender_2 (
    .in(spiralgen_1_y), .out(bit_extender_2_out));
  // Probe on bit_extender_1_out
  // Probe on bit_extender_2_out
  ROM #(.addrWidth(3), .dataWidth(4)) rom_1 (.addr(counter_1_q), .data(rom_1_data));  // open: sel
  assign bit_extender_3_out = {{10{rom_1_data[1]}}, rom_1_data[1:0]};  // Bit_Extender bit_extender_3
  assign bit_extender_4_out = {{10{rom_1_data[3]}}, rom_1_data[3:2]};  // Bit_Extender bit_extender_4
  Adder #(.width(12)) adder_1 (.a(bit_extender_3_out), .b(bit_extender_1_out), .out(adder_1_out));  // open: cin, cout
  Adder #(.width(12)) adder_2 (.a(bit_extender_4_out), .b(bit_extender_2_out), .out(adder_2_out));  // open: cin, cout
  Multiplexer #(.width(24), .enable("false")) multiplexer_1 (
    .in0({adder_2_out, adder_1_out}), .in1({bit_extender_2_out, bit_extender_1_out}),
    .out(multiplexer_1_out), .sel(j_k_ff_1_q));
  Comparator #(.width(24)) comparator_1 (
    .a({24{1'b0}}), .b({bit_extender_2_out, bit_extender_1_out}), .eq(comparator_1_eq));  // open: gt, lt
  and and_2 (and_2_out, comparator_1_eq, counter_1_carry);
  // Probe on in_1
  RAM #(.addrWidth(24), .dataWidth(32)) ram_1 (
    .addr(multiplexer_1_out), .data(out_3), .clk(clock_1_out), .ld(j_k_ff_1_qn), .clr(RST));  // open: sel
  Comparator #(.width(32)) comparator_2 (.a(in_1), .b(out_3), .lt(comparator_2_lt));  // open: gt, eq
  not not_1 (not_1_out, comparator_2_lt);
  Adder #(.width(32)) adder_3 (.a(out_3), .b(register_1_q), .out(adder_3_out), .cin(and_2_out));  // open: cout
  Multiplexer #(.width(32), .enable("false")) multiplexer_2 (
    .in0({32{1'b0}}), .in1(adder_3_out), .out(multiplexer_2_out), .sel(nand_1_out));
  nand nand_1 (nand_1_out, not_1_out, j_k_ff_1_q);
  // Probe on register_1_q
  Register #(.width(32)) register_1 (
    .D(multiplexer_2_out), .en(not_1_out), .Q(register_1_q), .clk(clock_1_out), .clr(RST));
  assign out_3 = j_k_ff_1_q ? register_1_q : 32'bz;  // Controlled_Buffer controlled_buffer_1
  // Probe on out_3

  // Notes on the sheet:
  //   contents of rom_1 (hex, n*v repeats v):
  //   f c d 1 5 4 7 3
endmodule

module day04ab (
  input  PartB,
  input  RST,
  output [31:0] out_3
);

  wire addr_carry, and_1_out, clock_1_out, comparator_1_eq, comparator_2_eq, comparator_2_gt,
       keyboard_1_avail, memAddr, multiplexer_5_out, nCond, not_2_out, or_1_out, xor_1_out;
  wire [1:0] condData, condSel, memData;
  wire [4:0] addr_q;
  wire [6:0] keyboard_1_data, multiplexer_1_out, multiplexer_3_out, multiplexer_4_out, ram_1_data, rCx_q;
  wire [7:0] regOp;
  wire [20:16] rom_1_data;
  wire [23:0] adder_1_out, multiplexer_2_out, not_1_out, rIo_q, rIx_q, rIy_q, shifter_1_out;

  Clock clock_1 (.out(clock_1_out));
  Keyboard keyboard_1 (.clk(clock_1_out), .re(regOp[7]), .clr(RST), .avail(keyboard_1_avail), .data(keyboard_1_data));
  Multiplexer #(.width(7), .enable("false")) multiplexer_1 (
    .in0(ram_1_data), .in1(keyboard_1_data), .out(multiplexer_1_out), .sel(regOp[7]));
  and and_1 (and_1_out, regOp[4], or_1_out);
  or or_1 (or_1_out, keyboard_1_avail, ~regOp[7]);  // OR_Gate
  Register #(.width(7)) rCx (.D(multiplexer_1_out), .en(regOp[6]), .Q(rCx_q), .clk(clock_1_out), .clr(RST));
  Counter #(.width(24), .max('hffffff)) rIx (
    .load(regOp[5]), .count(and_1_out), .Q(rIx_q), .clk(clock_1_out), .clr(RST));  // open: D, carry
  Counter #(.width(24), .max('hffffff)) rIy (
    .load(regOp[3]), .count(regOp[2]), .Q(rIy_q), .clk(clock_1_out), .clr(RST));  // open: D, carry
  Counter #(.width(24), .max('hffffff)) rIo (
    .load(regOp[1]), .count(regOp[0]), .Q(rIo_q), .clk(clock_1_out), .clr(RST));  // open: D, carry
  Multiplexer #(.width(24), .enable("false")) multiplexer_2 (
    .in0(rIx_q), .in1(rIy_q), .out(multiplexer_2_out), .sel(memAddr));
  // Probe on multiplexer_3_out
  Multiplexer #(.select(2), .width(7), .enable("false")) multiplexer_3 (
    .in0(rCx_q), .in1(multiplexer_1_out), .in2(7'b0100000), .in3(7'b0001010), .out(multiplexer_3_out),
    .sel(condData));
  Adder #(.width(24)) adder_1 (.a(rIo_q), .b(multiplexer_2_out), .out(adder_1_out));  // open: cin, cout
  Multiplexer #(.select(2), .width(7), .enable("false")) multiplexer_4 (
    .in0(multiplexer_1_out), .in1(rCx_q), .in2(7'b0100000), .in3(7'b0001010), .out(multiplexer_4_out),
    .sel(memData));
  // Probe on multiplexer_4_out
  Comparator #(.width(24)) comparator_1 (.a(rIx_q), .b(rIy_q), .eq(comparator_1_eq));  // open: gt, lt
  Comparator #(.width(7), .mode("unsigned")) comparator_2 (
    .a(multiplexer_1_out), .b(multiplexer_3_out), .gt(comparator_2_gt), .eq(comparator_2_eq));  // open: lt
  Multiplexer #(.select(2), .enable("false")) multiplexer_5 (
    .in0(comparator_1_eq), .in1(comparator_2_gt), .in2(comparator_2_eq), .in3(PartB),
    .out(multiplexer_5_out), .sel(condSel));
  RAM #(.addrWidth(24), .dataWidth(7), .bus("separate")) ram_1 (
    .addr(adder_1_out), .din(multiplexer_4_out), .data(ram_1_data), .clk(clock_1_out), .clr(RST));  // open: str, sel, ld
  DotMatrix #(.matrixcols(4), .matrixrows(24)) dotmatrix_1 (.col0(rIx_q), .col1(rIy_q), .col2(rIo_q), .col3(not_1_out));
  xor xor_1 (xor_1_out, multiplexer_5_out, nCond);
  assign not_1_out = ~shifter_1_out;  // NOT_Gate not_1, 24 bits wide
  Shifter #(.width(24)) shifter_1 (.in({24{1'b1}}), .\dist (addr_q), .out(shifter_1_out));
  Counter #(.width(5), .max('h1f)) addr (
    .load(xor_1_out), .D(rom_1_data), .count(not_2_out), .Q(addr_q), .carry(addr_carry), .clk(clock_1_out),
    .clr(RST));
  not not_2 (not_2_out, xor_1_out);
  Counter #(.width(32), .max('hffffffff)) res (
    .count(addr_carry), .Q(out_3), .clk(clock_1_out), .clr(RST));  // open: load, D, carry
  // Probe on out_3
  ROM #(.addrWidth(5), .dataWidth(21)) rom_1 (
    .addr(addr_q), .data({rom_1_data, memAddr, nCond, condSel, condData, memData, regOp}));  // open: sel

  // Notes on the sheet:
  //   contents of rom_1 (hex, n*v repeats v):
  //   1e642a 1e6610 26c90 1e6730 b7620 a2c00 52850 65000 1e6570 62530 1e6420 b6818 1f2c00 de804 b8400
  //   bac00 1e6440 14e000 2800 102401 d2402
endmodule

module day05ab (
  input  RST,
  input  Part_B,
  output [31:0] out_3
);

  wire and_1_out, and_2_out, and_3_out, clock_1_out, comparator_1_gt, comparator_2_lt, keyboard_1_avail,
       s_r_ff_1_q, s_r_ff_1_qn, ssvtokenizer_1_newlinep, ssvtokenizer_1_numberp, ssvtokenizer_1_read,
       ssvtokenizer_1_rst_2;
  wire [6:0] keyboard_1_data;
  wire [23:0] adder_1_out, adder_2_out, bit_extender_1_out, controlled_buffer_1_out, controlled_buffer_2_out,
       counter_1_q, ix_q, multiplexer_1_out, ram_1_data;
  wire [31:0] ssvtokenizer_1_number;

  Clock clock_1 (.out(clock_1_out));
  Keyboard keyboard_1 (
    .clk(clock_1_out), .re(ssvtokenizer_1_read), .clr(ssvtokenizer_1_rst_2), .avail(keyboard_1_avail),
    .data(keyboard_1_data));
  ssvTokenizer ssvtokenizer_1 (
    .ASCII(keyboard_1_data), .Available(keyboard_1_avail), .Clk(clock_1_out), .Rst(RST),
    .Read(ssvtokenizer_1_read), .NumberP(ssvtokenizer_1_numberp), .NewlineP(ssvtokenizer_1_newlinep),
    .Number(ssvtokenizer_1_number), .RST_2(ssvtokenizer_1_rst_2));  // open: TokenP, SpaceP, Enable
  S_R_Flip_Flop s_r_ff_1 (
    .S(ssvtokenizer_1_newlinep), .clk(clock_1_out), .R(RST), .Q(s_r_ff_1_q), .Qn(s_r_ff_1_qn), .reset(RST));  // open: preset, en
  and and_1 (and_1_out, s_r_ff_1_qn, ssvtokenizer_1_numberp);
  Bit_Extender #(.in_width(32), .out_width(24)) bit_extender_1 (.in(ssvtokenizer_1_number), .out(bit_extender_1_out));
  and and_2 (and_2_out, comparator_2_lt, s_r_ff_1_q);
  Counter #(.width(24), .max('hffffff)) counter_1 (
    .count(and_1_out), .Q(counter_1_q), .clk(clock_1_out), .clr(RST));  // open: load, D, carry
  assign controlled_buffer_1_out = and_2_out ? ix_q : 24'bz;  // Controlled_Buffer controlled_buffer_1
  assign controlled_buffer_2_out = and_2_out ? adder_2_out : 24'bz;  // Controlled_Buffer controlled_buffer_2
  assign controlled_buffer_2_out = s_r_ff_1_qn ? bit_extender_1_out : 24'bz;  // Controlled_Buffer controlled_buffer_3
  assign controlled_buffer_1_out = s_r_ff_1_qn ? counter_1_q : 24'bz;  // Controlled_Buffer controlled_buffer_4
  RAM #(.addrWidth(24), .dataWidth(24), .bus("separate")) ram_1 (
    .addr(controlled_buffer_1_out), .din(controlled_buffer_2_out), .data(ram_1_data), .clk(clock_1_out),
    .clr(RST));  // open: str, sel, ld
  Adder #(.width(24)) adder_1 (.a(ix_q), .b(ram_1_data), .out(adder_1_out));  // open: cin, cout
  Comparator #(.width(24)) comparator_1 (.a(ram_1_data), .b(24'h2), .gt(comparator_1_gt));  // open: eq, lt
  Register #(.width(24)) ix (.D(adder_1_out), .en(and_2_out), .Q(ix_q), .clk(clock_1_out), .clr(RST));
  Multiplexer #(.width(24), .enable("false")) multiplexer_1 (
    .in0(24'h1), .in1({24{1'b1}}), .out(multiplexer_1_out), .sel(and_3_out));
  and and_3 (and_3_out, comparator_1_gt, Part_B);
  Comparator #(.width(24), .mode("unsigned")) comparator_2 (
    .a(ix_q), .b(counter_1_q), .lt(comparator_2_lt));  // open: gt, eq
  Adder #(.width(24)) adder_2 (.a(ram_1_data), .b(multiplexer_1_out), .out(adder_2_out));  // open: cin, cout
  Counter #(.width(32), .max('hffffffff)) res (
    .count(and_2_out), .Q(out_3), .clk(clock_1_out), .clr(RST));  // open: load, D, carry
  // Probe on out_3
endmodule

module day06ab (
  input  RST,
  output [15:0] PartA,
  output [15:0] PartB
);

  wire addr_carry, AddrX, and_1_out, and_2_out, clock_1_out, comparator_4_gt, eq32, gt32, kbNl,
       keyboard_1_avail, kludge, memLd, multiplexer_8_out, not_1_out, not_2_out, or_1_out, rNmCt, rNmEn,
       rnmv, rNxEn, rXmEn, rXmXx, rXwEn, rxxd, rXxEn, rXxLd, rxxv, rXxXm, rYhEn, rYxEn, ryxv,
       ssvtokenizer_1_numberp, ssvtokenizer_1_read, ssvtokenizer_1_rst_2, xor_1_out;
  wire [1:0] AddrY, dcmux;
  wire [3:0] addr_q;
  wire [6:0] keyboard_1_data;
  wire [7:0] adder_1_out, multiplexer_1_out, multiplexer_2_out, multiplexer_3_out, multiplexer_4_out, rXm_q,
       rXw_q, rXx_q;
  wire [15:0] adder_3_out, multiplexer_5_out, multiplexer_7_out, rYh_q, rYx_q, subtractor_1_out;
  wire [19:12] rom_1_data;
  wire [31:0] adder_2_out, multiplexer_6_out, ram_1_data, rNm_q, rNx_q, ssvtokenizer_1_number;

  Clock clock_1 (.out(clock_1_out));
  Multiplexer #(.width(8), .enable("false")) multiplexer_1 (
    .in0({8{1'b0}}), .in1(rXm_q), .out(multiplexer_1_out), .sel(rXxXm));
  or or_1 (or_1_out, rXxLd, rxxv);
  Keyboard keyboard_1 (
    .clk(clock_1_out), .re(ssvtokenizer_1_read), .clr(ssvtokenizer_1_rst_2), .avail(keyboard_1_avail),
    .data(keyboard_1_data));
  ssvTokenizer ssvtokenizer_1 (
    .ASCII(keyboard_1_data), .Available(keyboard_1_avail), .Clk(clock_1_out), .Rst(RST),
    .Read(ssvtokenizer_1_read), .NumberP(ssvtokenizer_1_numberp), .NewlineP(kbNl),
    .Number(ssvtokenizer_1_number), .RST_2(ssvtokenizer_1_rst_2), .Enable(rXwEn));  // open: TokenP, SpaceP
  Counter rXw (.count(and_1_out), .Q(rXw_q), .clk(clock_1_out), .clr(RST));  // open: load, D, carry
  and and_1 (and_1_out, ssvtokenizer_1_numberp, rXwEn);
  Multiplexer #(.width(8), .enable("false")) multiplexer_2 (
    .in0(adder_1_out), .in1(multiplexer_1_out), .out(multiplexer_2_out), .sel(or_1_out));
  Register rXx (.D(multiplexer_2_out), .en(rXxEn), .Q(rXx_q), .clk(clock_1_out), .clr(RST));
  Register rXm (.D(multiplexer_3_out), .en(rXmEn), .Q(rXm_q), .clk(clock_1_out), .clr(RST));
  Multiplexer #(.width(8), .enable("false")) multiplexer_3 (
    .in0({8{1'b0}}), .in1(rXx_q), .out(multiplexer_3_out), .sel(rXmXx));
  Adder adder_1 (.a(rXx_q), .b({8{1'b0}}), .out(adder_1_out), .cin(1'b1));  // open: cout
  Comparator comparator_1 (.a(rXm_q), .b(rXx_q), .gt(kludge));  // open: eq, lt
  Multiplexer #(.width(8), .enable("false")) multiplexer_4 (
    .in0(rXw_q), .in1(rXx_q), .out(multiplexer_4_out), .sel(AddrX));
  Comparator comparator_2 (.a(rXw_q), .b(adder_1_out), .eq(rxxv));  // open: gt, lt
  D_Flip_Flop #(.trigger("high")) d_ff_1 (.clk(clock_1_out), .D(rxxv), .Q(rxxd), .reset(RST));  // open: Qn, preset, en
  Register #(.width(32)) rNx (.D(multiplexer_6_out), .en(rNxEn), .Q(rNx_q), .clk(clock_1_out), .clr(RST));
  Counter #(.width(32), .max('hffffffff)) rNm (
    .load(rNmEn), .D(multiplexer_6_out), .count(rNmCt), .Q(rNm_q), .carry(rnmv), .clk(clock_1_out), .clr(RST));
  Counter #(.width(16), .max('hffff)) rYh (
    .count(rYhEn), .Q(rYh_q), .clk(clock_1_out), .clr(RST));  // open: load, D, carry
  Register #(.width(16)) rYx (.D(multiplexer_5_out), .en(rYxEn), .Q(rYx_q), .clk(clock_1_out), .clr(RST));
  Multiplexer #(.width(16), .enable("false")) multiplexer_5 (
    .in0(adder_3_out), .in1({16{1'b0}}), .out(multiplexer_5_out), .sel(ryxv));
  // Probe on ram_1_data
  RAM #(.addrWidth(24), .dataWidth(32)) ram_1 (
    .addr({multiplexer_7_out, multiplexer_4_out}), .data(ram_1_data), .clk(clock_1_out), .ld(memLd), .clr(RST));  // open: sel
  assign ram_1_data = not_1_out ? multiplexer_6_out : 32'bz;  // Controlled_Buffer controlled_buffer_1
  not not_1 (not_1_out, memLd);
  Adder #(.width(32)) adder_2 (.a(rNx_q), .b(32'h1), .out(adder_2_out));  // open: cin, cout
  Adder #(.width(16)) adder_3 (.a(rYx_q), .b({16{1'b0}}), .out(adder_3_out), .cin(1'b1));  // open: cout
  Multiplexer #(.select(2), .width(32), .enable("false")) multiplexer_6 (
    .in0(ssvtokenizer_1_number), .in1(ram_1_data), .in2(rNm_q), .in3(adder_2_out), .out(multiplexer_6_out),
    .sel(dcmux));
  Multiplexer #(.select(2), .width(16), .enable("false")) multiplexer_7 (
    .in0({16{1'b1}}), .in2(rYx_q), .in3(rYh_q), .out(multiplexer_7_out), .sel(AddrY));  // open: in1
  Subtractor #(.width(16)) subtractor_1 (.a(rYh_q), .b(rYx_q), .out(subtractor_1_out));  // open: bin, bout
  Comparator #(.width(16)) comparator_3 (.a(rYh_q), .b(adder_3_out), .eq(ryxv));  // open: gt, lt
  Comparator #(.width(32)) comparator_4 (
    .a(ram_1_data), .b(multiplexer_6_out), .gt(comparator_4_gt), .eq(eq32));  // open: lt
  // Probe on multiplexer_6_out
  assign PartA = addr_carry ? rYh_q : 16'bz;  // Controlled_Buffer controlled_buffer_2
  and and_2 (and_2_out, kludge, eq32);
  or or_2 (gt32, and_2_out, comparator_4_gt);
  // Probe on PartA
  assign PartB = addr_carry ? subtractor_1_out : 16'bz;  // Controlled_Buffer controlled_buffer_3
  // Probe on PartB
  Multiplexer #(.select(3), .enable("false")) multiplexer_8 (
    .in0(rxxv), .in1(kbNl), .in2(rxxd), .in3(gt32), .in4(ryxv), .in5(eq32), .in6(rnmv), .in7(1'b1),
    .out(multiplexer_8_out), .sel(rom_1_data[14:12]));
  xor xor_1 (xor_1_out, multiplexer_8_out, rom_1_data[15]);
  // Probe on rom_1_data[19:16]
  not not_2 (not_2_out, xor_1_out);
  Counter #(.width(4), .max('hf)) addr (
    .load(xor_1_out), .D(rom_1_data[19:16]), .count(not_2_out), .Q(addr_q), .carry(addr_carry),
    .clk(clock_1_out), .clr(RST));
  ROM #(.addrWidth(4), .dataWidth(25)) rom_1 (
    .addr(addr_q),
    .data({dcmux, AddrY, AddrX, rom_1_data, rYxEn, rYhEn, rNmCt, rNmEn, rNxEn, memLd, rXmEn, rXmXx, rXxEn, rXxLd, rXxXm, rXwEn}));  // open: sel

  // Notes on the sheet:
  //   The built-in keyboard can't handle tabs, so use spaces instead
  //   contents of rom_1 (hex, n*v repeats v):
  //   9001 9ff170 1718008 115b040 9ff170 38048 ff04e 1ff008 9e63c0 1987008 ff44c 9f2140 15b5048 bc84c
  //   17040 f7000
endmodule

module day07a (
  input  Read,
  input  RST
);

  wire and_1_out, and_2_out, clock_1_out, keyboard_1_avail, or_1_out;
  wire [6:0] keyboard_1_data, ram_1_data, xor_1_out;
  wire [23:0] addr_q;

  Clock clock_1 (.out(clock_1_out));
  Keyboard keyboard_1 (.clk(clock_1_out), .clr(RST), .avail(keyboard_1_avail), .data(keyboard_1_data));  // open: re
  and and_1 (and_1_out, keyboard_1_data[5], keyboard_1_data[6]);
  and and_2 (and_2_out, keyboard_1_avail, ~and_1_out);  // AND_Gate
  or or_1 (or_1_out, and_1_out, Read);
  Counter #(.width(24), .max('hffffff)) addr (
    .load(and_2_out), .count(or_1_out), .Q(addr_q), .clk(clock_1_out), .clr(RST));  // open: D, carry
  assign xor_1_out = ram_1_data ^ keyboard_1_data;  // XOR_Gate xor_1, 7 bits wide
  RAM #(.addrWidth(24), .dataWidth(7), .bus("separate")) ram_1 (
    .addr(addr_q), .din(xor_1_out), .data(ram_1_data), .str(and_1_out), .clk(clock_1_out), .clr(RST));  // open: sel, ld
  TTY tty_1 (.data(ram_1_data), .clk(clock_1_out), .we(Read), .clr(RST));
endmodule
